# Fritzing sketch Wiring Picture (saved by Fritzing 0.9.3b)

parts:
  元件1 = Arduino Nano (Rev3.0)
  S2 = Round Pushbutton
  S3 = Round Pushbutton
  S4 = Round Pushbutton
  S5 = Round Pushbutton
  S6 = Round Pushbutton
  S7 = Round Pushbutton
  S8 = Round Pushbutton
  S9 = Round Pushbutton
  S10 = Round Pushbutton
  S11 = Round Pushbutton
  S13 = Round Pushbutton
  S14 = Round Pushbutton
  S15 = Round Pushbutton
  S16 = Round Pushbutton
  元件2 = NRF24L01+ Breakout Board
  U1 = ENCODER_2LED [package=encoder_led_2]
  U2 = ENCODER_2LED [package=encoder_led_2]  # not connected
  U3 = ENCODER_2LED [package=encoder_led_2]  # not connected
  U4 = ENCODER_2LED [package=encoder_led_2]  # not connected
  U5 = V_REG_LD1117VXX [package=78xxl]
  元件3 = USB LiPoly Charger
  VCC1 = Battery

nets:
  GND: 元件1.GND, 元件2.GND, 元件3.GND, VCC1.-
  N1: 元件1.D4, S2.leg0, S11.leg0, S16.leg0
  N2: 元件1.D5, S3.leg0
  N3: 元件1.D6, S4.leg0
  N4: 元件1.D7, S5.leg0, S8.leg0, S13.leg0
  N5: 元件1.D8, S6.leg0, S7.leg0, U1.C
  N6: 元件1.D9, 元件2.CE
  N7: 元件1.D10, 元件2.CS
  N8: 元件1.D11/MOSI, 元件2.MOSI
  N9: 元件1.D12/MISO, 元件2.MISO
  N10: 元件1.VIN, 元件3.VBAT, VCC1.+
  N11: 元件1.5V, U5.IN
  N12: 元件1.A2, S13.leg1, S14.leg1, S15.leg1, S16.leg1
  N13: 元件1.A1, S6.leg1, S8.leg1, S9.leg1, S10.leg1, S11.leg1
  N14: 元件1.A0, S2.leg1, S3.leg1, S4.leg1, S5.leg1, S7.leg1
  N15: 元件1.D13/SCK, 元件2.SCK
  N16: S9.leg0, S14.leg0
  N17: S10.leg0, S15.leg0
  N18: 元件2.VCC, U5.OUT

custom parts:
  ENCODER_2LED: Illuminated Rotary Encoder w/ 2 LEDs
